// Logisim project Test_Circuit3_DD1_Proj1.circ as structural Verilog: 1 circuit, main circuit main
module main (
  input  in_1,
  input  in_2,
  input  in_3,
  output out_4
);

  wire and_1_out, and_2_out, nor_1_out, not_1_out, not_2_out;

  not not_1 (not_1_out, in_1);
  not not_2 (not_2_out, in_3);
  and and_1 (and_1_out, not_1_out, in_3, in_2);
  nor nor_1 (nor_1_out, in_2, in_3);
  and and_2 (and_2_out, in_2, not_2_out, in_1);
  or or_1 (out_4, and_1_out, nor_1_out, and_2_out);
endmodule
